// Logisim project Sagui_vet.circ as structural Verilog: 5 circuits, main circuit main
module main (
);

  wire branch, button_1_out, clk, mv, not_1_out, ram_w, writeEn;
  wire [1:0] multiplexer_4_out, mvSel;
  wire [3:0] func, Imm;
  wire [7:0] adder_1_out, alu_8bits_1_s, B, banco_registradores_1_a, C, Control_Mem_data, multiplexer_1_out,
       multiplexer_3_out, nor_1_out, PC_q, r0, r1, r2, r3, Seq_Data_Mem_dout;
  wire [7:5] Instruction_Mem_data;

  Adder adder_1 (.a(PC_q), .b(8'h1), .out(adder_1_out));  // open: cin, cout
  Register PC (.D(multiplexer_1_out), .en(1'b1), .clk(clk), .Q(PC_q), .clr(button_1_out));
  Multiplexer #(.width(8)) multiplexer_1 (.in0(adder_1_out), .in1(B), .out(multiplexer_1_out), .sel(branch));
  Clock clock_1 (.out(clk));
  ROM Instruction_Mem (.addr(PC_q), .data({Instruction_Mem_data, Instruction_Mem_data[5], Imm}));
  Button button_1 (.out(button_1_out));
  Multiplexer multiplexer_2 (.sel(Instruction_Mem_data[7]));  // open: in0, in1, out
  ROM #(.addrWidth(4)) Control_Mem (.addr({Instruction_Mem_data, Instruction_Mem_data[5]}), .data(Control_Mem_data));
  not not_1 (not_1_out, mv);
  Multiplexer #(.width(8)) multiplexer_3 (.in0({4'b0000, Imm}), .in1(C), .out(multiplexer_3_out), .sel(not_1_out));
  Multiplexer #(.width(2)) multiplexer_4 (.in0(Imm[3:2]), .in1(2'b01), .out(multiplexer_4_out), .sel(mv));
  banco_registradores banco_registradores_1 (
    .rrb(Imm[1:0]), .rra(Imm[3:2]), .Clk(clk), .En(writeEn), .mv(mvSel), .C(multiplexer_3_out),
    .wr(multiplexer_4_out), .B(B), .A(banco_registradores_1_a), .r2(r2), .r0(r0), .r1(r1), .r3(r3));
  id id_1 ();  // open: rra, clk, rrb, A, B
  banco_registradores_vet banco_registradores_vet_1 ();  // open: C, Clk, En, wr, mv, rra, rrb, r0, r1, A, r2, B, r3
  banco_registradores_vet banco_registradores_vet_2 ();  // open: C, Clk, En, wr, mv, rra, rrb, r0, r1, A, r2, B, r3
  banco_registradores_vet banco_registradores_vet_3 ();  // open: C, Clk, En, wr, mv, rra, rrb, r0, r1, A, r2, B, r3
  assign nor_1_out = ~({8{1'b0}} | banco_registradores_1_a);  // NOR_Gate nor_1, 8 bits wide
  RAM Seq_Data_Mem (
    .addr(banco_registradores_1_a), .we(ram_w), .oe(1'b1), .clk(clk), .din(B), .dout(Seq_Data_Mem_dout));
  and and_1 (branch, nor_1_out[0], nor_1_out[1], nor_1_out[2], nor_1_out[3], nor_1_out[4], nor_1_out[5], nor_1_out[6], nor_1_out[7]);
  ALU_8bits alu_8bits_1 (.A(banco_registradores_1_a), .func(func), .B(B), .S(alu_8bits_1_s));  // open: Zero
  Multiplexer #(.width(8)) multiplexer_5 (.in0(alu_8bits_1_s), .in1(Seq_Data_Mem_dout), .out(C));  // open: sel

  // Other names for the same wires on the sheet: rb[1:0] = Imm[1:0]; ra[1:0] = Imm[3:2]
endmodule

module banco_registradores (
  input  [7:0] C,
  input  Clk,
  input  En,
  input  [1:0] wr,
  input  [1:0] mv,
  input  [1:0] rra,
  input  [1:0] rrb,
  output [7:0] r0,
  output [7:0] r1,
  output [7:0] A,
  output [7:0] r2,
  output [7:0] B,
  output [7:0] r3
);

  wire and_1_out, and_2_out, and_3_out, and_4_out, and_5_out, and_6_out, and_7_out, and_8_out, and_9_out,
       and_10_out, and_11_out, and_12_out, demultiplexer_1_out0, demultiplexer_1_out1, demultiplexer_1_out2,
       demultiplexer_1_out3, not_1_out, not_2_out, not_3_out, not_4_out, not_5_out, not_6_out, not_7_out,
       not_8_out, not_9_out, or_1_out, or_2_out, or_3_out, or_4_out, or_5_out, or_6_out;
  wire [3:0] high;

  Demultiplexer #(.select(2)) demultiplexer_1 (
    .out0(demultiplexer_1_out0), .out1(demultiplexer_1_out1), .out2(demultiplexer_1_out2),
    .out3(demultiplexer_1_out3), .in(En), .sel(wr));
  Multiplexer #(.width(4)) multiplexer_1 (.in0(C[7:4]), .in1(C[3:0]), .out(high), .sel(mv[1]));
  not not_1 (not_1_out, mv[1]);
  and and_1 (and_1_out, not_1_out, demultiplexer_1_out1);
  and and_2 (and_2_out, demultiplexer_1_out1, mv[0]);
  not not_2 (not_2_out, mv[1]);
  and and_3 (and_3_out, not_2_out, demultiplexer_1_out1);
  and and_4 (and_4_out, demultiplexer_1_out1, not_3_out);
  not not_3 (not_3_out, mv[0]);
  not not_4 (not_4_out, mv[1]);
  and and_5 (and_5_out, not_4_out, demultiplexer_1_out2);
  and and_6 (and_6_out, demultiplexer_1_out2, mv[0]);
  not not_5 (not_5_out, mv[1]);
  and and_7 (and_7_out, not_5_out, demultiplexer_1_out2);
  and and_8 (and_8_out, demultiplexer_1_out2, not_6_out);
  not not_6 (not_6_out, mv[0]);
  not not_7 (not_7_out, mv[1]);
  and and_9 (and_9_out, not_7_out, demultiplexer_1_out3);
  and and_10 (and_10_out, demultiplexer_1_out3, mv[0]);
  not not_8 (not_8_out, mv[1]);
  and and_11 (and_11_out, not_8_out, demultiplexer_1_out3);
  and and_12 (and_12_out, demultiplexer_1_out3, not_9_out);
  not not_9 (not_9_out, mv[0]);
  or or_1 (or_1_out, and_1_out, and_2_out);
  or or_2 (or_2_out, and_3_out, and_4_out);
  or or_3 (or_3_out, and_5_out, and_6_out);
  or or_4 (or_4_out, and_7_out, and_8_out);
  or or_5 (or_5_out, and_9_out, and_10_out);
  or or_6 (or_6_out, and_11_out, and_12_out);
  Register #(.trigger("falling"), .width(4)) register_1 (.D(4'b0000), .en(1'b0), .clk(Clk), .Q(r0[7:4]));  // open: clr
  Register #(.trigger("falling"), .width(4)) register_2 (.D(4'b0000), .en(1'b0), .clk(Clk), .Q(r0[3:0]));  // open: clr
  Register #(.trigger("falling"), .width(4)) register_3 (.D(high), .en(or_1_out), .clk(Clk), .Q(r1[7:4]));  // open: clr
  Register #(.trigger("falling"), .width(4)) register_4 (
    .D(C[3:0]), .en(or_2_out), .clk(Clk), .Q(r1[3:0]));  // open: clr
  Register #(.trigger("falling"), .width(4)) register_5 (.D(high), .en(or_3_out), .clk(Clk), .Q(r2[7:4]));  // open: clr
  Register #(.trigger("falling"), .width(4)) register_6 (
    .D(C[3:0]), .en(or_4_out), .clk(Clk), .Q(r2[3:0]));  // open: clr
  Register #(.trigger("falling"), .width(4)) register_7 (.D(high), .en(or_5_out), .clk(Clk), .Q(r3[7:4]));  // open: clr
  Register #(.trigger("falling"), .width(4)) register_8 (
    .D(C[3:0]), .en(or_6_out), .clk(Clk), .Q(r3[3:0]));  // open: clr
  Multiplexer #(.select(2), .width(8)) multiplexer_2 (.in0(r0), .in1(r1), .in2(r2), .in3(r3), .out(A), .sel(rra));
  Multiplexer #(.select(2), .width(8)) multiplexer_3 (.in0(r0), .in1(r1), .in2(r2), .in3(r3), .out(B), .sel(rrb));
  // also tied to GND on the sheet: demultiplexer_1_out0

  // Other names for the same wires on the sheet: low[3:0] = C[3:0]; mvSel = mv[0]; mv_t = mv[1]
endmodule

module ALU_8bits (
  input  [7:0] A,
  input  [3:0] func,
  input  [7:0] B,
  output Zero,
  output [7:0] S
);

  wire or_1_out;
  wire [7:0] adder_1_out, and_1_out, subtractor_1_out;

  Adder adder_1 (.a(A), .b(B), .out(adder_1_out));  // open: cin, cout
  Subtractor subtractor_1 (.a(A), .b(B), .out(subtractor_1_out));  // open: bin, bout
  assign and_1_out = A & B;  // AND_Gate and_1, 8 bits wide
  Multiplexer #(.select(4), .width(8)) multiplexer_1 (
    .in0(adder_1_out), .in1(subtractor_1_out), .in2(and_1_out), .out(S), .sel(func));  // open: in3, in4, in5, in6, in7, in8, in9, in10, in11, in12, in13, in14, in15
  or or_1 (or_1_out, S[0], S[1], S[2], S[3], S[4], S[5], S[6], S[7]);
  not not_1 (Zero, or_1_out);
endmodule

module banco_registradores_vet (
  input  [7:0] C,
  input  Clk,
  input  En,
  input  [1:0] wr,
  input  [1:0] mv,
  input  [1:0] rra,
  input  [1:0] rrb,
  output [7:0] r0,
  output [7:0] r1,
  output [7:0] A,
  output [7:0] r2,
  output [7:0] B,
  output [7:0] r3
);

  wire and_1_out, and_2_out, and_3_out, and_4_out, and_5_out, and_6_out, and_7_out, and_8_out, and_9_out,
       and_10_out, and_11_out, and_12_out, and_13_out, and_14_out, and_15_out, and_16_out,
       demultiplexer_1_out0, demultiplexer_1_out1, demultiplexer_1_out2, demultiplexer_1_out3, not_1_out,
       not_2_out, not_3_out, not_4_out, not_5_out, not_6_out, not_7_out, not_8_out, not_9_out, not_10_out,
       not_11_out, not_12_out, or_1_out, or_2_out, or_3_out, or_4_out, or_5_out, or_6_out, or_7_out, or_8_out;
  wire [3:0] high;

  Demultiplexer #(.select(2)) demultiplexer_1 (
    .out0(demultiplexer_1_out0), .out1(demultiplexer_1_out1), .out2(demultiplexer_1_out2),
    .out3(demultiplexer_1_out3), .in(En), .sel(wr));
  Multiplexer #(.width(4)) multiplexer_1 (.in0(C[7:4]), .in1(C[3:0]), .out(high), .sel(mv[1]));
  not not_1 (not_1_out, mv[1]);
  and and_1 (and_1_out, not_1_out, demultiplexer_1_out0);
  and and_2 (and_2_out, demultiplexer_1_out0, mv[0]);
  not not_2 (not_2_out, mv[1]);
  and and_3 (and_3_out, not_2_out, demultiplexer_1_out0);
  and and_4 (and_4_out, demultiplexer_1_out0, not_3_out);
  not not_3 (not_3_out, mv[0]);
  not not_4 (not_4_out, mv[1]);
  and and_5 (and_5_out, not_4_out, demultiplexer_1_out1);
  and and_6 (and_6_out, demultiplexer_1_out1, mv[0]);
  not not_5 (not_5_out, mv[1]);
  and and_7 (and_7_out, not_5_out, demultiplexer_1_out1);
  and and_8 (and_8_out, demultiplexer_1_out1, not_6_out);
  not not_6 (not_6_out, mv[0]);
  not not_7 (not_7_out, mv[1]);
  and and_9 (and_9_out, not_7_out, demultiplexer_1_out2);
  and and_10 (and_10_out, demultiplexer_1_out2, mv[0]);
  not not_8 (not_8_out, mv[1]);
  and and_11 (and_11_out, not_8_out, demultiplexer_1_out2);
  and and_12 (and_12_out, demultiplexer_1_out2, not_9_out);
  not not_9 (not_9_out, mv[0]);
  not not_10 (not_10_out, mv[1]);
  and and_13 (and_13_out, not_10_out, demultiplexer_1_out3);
  and and_14 (and_14_out, demultiplexer_1_out3, mv[0]);
  not not_11 (not_11_out, mv[1]);
  and and_15 (and_15_out, not_11_out, demultiplexer_1_out3);
  and and_16 (and_16_out, demultiplexer_1_out3, not_12_out);
  not not_12 (not_12_out, mv[0]);
  or or_1 (or_1_out, and_1_out, and_2_out);
  or or_2 (or_2_out, and_3_out, and_4_out);
  or or_3 (or_3_out, and_5_out, and_6_out);
  or or_4 (or_4_out, and_7_out, and_8_out);
  or or_5 (or_5_out, and_9_out, and_10_out);
  or or_6 (or_6_out, and_11_out, and_12_out);
  or or_7 (or_7_out, and_13_out, and_14_out);
  or or_8 (or_8_out, and_15_out, and_16_out);
  Register #(.trigger("falling"), .width(4)) register_1 (.D(high), .en(or_1_out), .clk(Clk), .Q(r0[7:4]));  // open: clr
  Register #(.trigger("falling"), .width(4)) register_2 (
    .D(C[3:0]), .en(or_2_out), .clk(Clk), .Q(r0[3:0]));  // open: clr
  Register #(.trigger("falling"), .width(4)) register_3 (.D(high), .en(or_3_out), .clk(Clk), .Q(r1[7:4]));  // open: clr
  Register #(.trigger("falling"), .width(4)) register_4 (
    .D(C[3:0]), .en(or_4_out), .clk(Clk), .Q(r1[3:0]));  // open: clr
  Register #(.trigger("falling"), .width(4)) register_5 (.D(high), .en(or_5_out), .clk(Clk), .Q(r2[7:4]));  // open: clr
  Register #(.trigger("falling"), .width(4)) register_6 (
    .D(C[3:0]), .en(or_6_out), .clk(Clk), .Q(r2[3:0]));  // open: clr
  Register #(.trigger("falling"), .width(4)) register_7 (.D(high), .en(or_7_out), .clk(Clk), .Q(r3[7:4]));  // open: clr
  Register #(.trigger("falling"), .width(4)) register_8 (
    .D(C[3:0]), .en(or_8_out), .clk(Clk), .Q(r3[3:0]));  // open: clr
  Multiplexer #(.select(2), .width(8)) multiplexer_2 (.in0(r0), .in1(r1), .in2(r2), .in3(r3), .out(A), .sel(rra));
  Multiplexer #(.select(2), .width(8)) multiplexer_3 (.in0(r0), .in1(r1), .in2(r2), .in3(r3), .out(B), .sel(rrb));

  // Other names for the same wires on the sheet: low[3:0] = C[3:0]; mvSel = mv[0]; mv_t = mv[1]
endmodule

module id (
  input  [1:0] rra,
  input  clk,
  input  [1:0] rrb,
  output [7:0] A,
  output [7:0] B
);

  wire [7:0] register_1_q, register_2_q, register_3_q, register_4_q;

  Register #(.trigger("falling")) register_1 (.D({8{1'b0}}), .en(1'b1), .clk(clk), .Q(register_1_q));  // open: clr
  Register #(.trigger("falling")) register_2 (.D(8'h1), .en(1'b1), .clk(clk), .Q(register_2_q));  // open: clr
  Register #(.trigger("falling")) register_3 (.D(8'h2), .en(1'b1), .clk(clk), .Q(register_3_q));  // open: clr
  Register #(.trigger("falling")) register_4 (.D(8'h3), .en(1'b1), .clk(clk), .Q(register_4_q));  // open: clr
  Multiplexer #(.select(2), .width(8)) multiplexer_1 (
    .in0(register_1_q), .in1(register_2_q), .in2(register_3_q), .in3(register_4_q), .out(A), .sel(rra));
  Multiplexer #(.select(2), .width(8)) multiplexer_2 (
    .in0(register_1_q), .in1(register_2_q), .in2(register_3_q), .in3(register_4_q), .out(B), .sel(rrb));
endmodule
